# Fritzing sketch Problem 1 Circuit (saved by Fritzing 0.9.3b)
breadboards: 1

parts:
  part = KY-032 IR Obstacle Avoidance Sensor Module [package="Breakout board"]
  part_2 = MH-ET LIVE ESP32 DEVKIT 38 pins
  R1 = PHOTOCELL [package=photocell]
  part_3 = Resistor [tolerance=±5% resistance=220 package="0603 [SMD]"]
  part_4 = Basic Servo

nets:
  GND: part.GND, part_2.GND, part_3.Pin_0, part_4.gnd
  3V3: part.+, part_2.3V3, part_2.IO19, R1.P$2, part_4.vcc
  N1: part.out, part_2.IO15
  N2: part_2.IO2, part_4.pulse
  N3: R1.P$1, part_3.Pin_1

custom parts:
  KY-032 IR Obstacle Avoidance Sensor Module: KY-032 Infrared Obstacle Avoidance Sensor. Distance-adjustable, infrared proximity sensor designed for wheeled robots. Also known as AD-032.
  MH-ET LIVE ESP32 DEVKIT 38 pins: http://mh.nodebb.com/topic/2/mh-et-live-esp32-devkit
