# Fritzing sketch Bar led (saved by Fritzing 0.9.3b)
breadboards: 1

parts:
  LED1 = LED - 5mm [color="Red (633nm)" package="5 mm [THT]"]
  LED2 = LED - 5mm [color="Yellow (585nm)" package="5 mm [THT]"]
  LED3 = LED - 5mm [color="Blue (430nm)" package="5 mm [THT]"]
  LED4 = LED - 5mm [color="Green (555nm)" package="5 mm [THT]"]
  LED5 = LED - 5mm [color="Orange (620nm)" package="5 mm [THT]"]
  R1 = Resistor [tolerance=±5% resistance=220 package=THT]
  R2 = Resistor [tolerance=±5% resistance=220 package=THT]
  R6 = Resistor [tolerance=±5% resistance=220 package=THT]
  R7 = Resistor [tolerance=±5% resistance=220 package=THT]
  R8 = Resistor [tolerance=±5% resistance=220 package=THT]
  part = MH-ET LIVE ESP32 DEVKIT 38 pins
  R10 = Rotary Potentiometer (Large) [maximum_resistance=100kΩ package=THT]

nets:
  N1: LED1.cathode, R1.Pin_1
  N2: LED1.anode, part.IO19
  N3: LED2.cathode, R2.Pin_1
  N4: LED2.anode, part.IO18
  N5: LED3.cathode, R6.Pin_1
  N6: LED3.anode, part.IO17
  N7: LED4.cathode, R7.Pin_1
  N8: LED4.anode, part.IO16
  N9: LED5.cathode, R8.Pin_1
  N10: LED5.anode, part.IO4
  N11: R1.Pin_0, R2.Pin_0, R6.Pin_0, R7.Pin_0, R8.Pin_0, part.GND, R10.leg1
  N12: part.5V, R10.leg2
  N13: part.IO5, R10.wiper

custom parts:
  MH-ET LIVE ESP32 DEVKIT 38 pins: http://mh.nodebb.com/topic/2/mh-et-live-esp32-devkit
