# Fritzing sketch Door (saved by Fritzing 0.9.3b)
breadboards: 1

parts:
  part = MH-ET LIVE ESP32 DEVKIT 38 pins
  Mod1 = KY-032 IR Obstacle Avoidance Sensor Module [package="Breakout board"]
  J1 = Basic Servo

nets:
  3V3: part.3V3, Mod1.+, J1.vcc
  N1: part.IO25, J1.pulse
  N2: part.IO26, Mod1.out
  GND: part.GND, Mod1.GND, J1.gnd

custom parts:
  MH-ET LIVE ESP32 DEVKIT 38 pins: http://mh.nodebb.com/topic/2/mh-et-live-esp32-devkit
  KY-032 IR Obstacle Avoidance Sensor Module: KY-032 Infrared Obstacle Avoidance Sensor. Distance-adjustable, infrared proximity sensor designed for wheeled robots. Also known as AD-032.
