# Fritzing sketch Flame (saved by Fritzing 0.9.3b)
breadboards: 1

parts:
  part = Resistor [tolerance=±5% resistance=220 package=THT]
  part_2 = LED - 5mm [color="Red (633nm)" package="5 mm [THT]"]
  part_3 = MH-ET LIVE ESP32 DEVKIT 38 pins
  T1 = TMP36 Temperature Sensor [package="TO92 [THT]"]
  part_4 = Piezo Speaker

nets:
  GND: part.Pin_0, part_3.GND, part_3.IO5, T1.GND, part_4.pin1, part_4.pin2
  N1: part.Pin_1, part_2.cathode
  N2: part_2.anode, part_3.IO2
  N3: part_3.3V3, T1.+Vs
  N4: part_3.IO34, T1.Vout

custom parts:
  MH-ET LIVE ESP32 DEVKIT 38 pins: http://mh.nodebb.com/topic/2/mh-et-live-esp32-devkit
