# Fritzing sketch 4x4 keypad (saved by Fritzing 0.9.3b)
breadboards: 1

parts:
  J1 = female pin header, 8 pins [form="♀ (female)"]
  Keypad4x1 = Keypad Membran 4x4
  MH-ET_LIVE_ESP32_DEVKIT1 = MH-ET LIVE ESP32 DEVKIT 38 pins
  J2 = Basic Servo

nets:
  N1: J1.pin1, Keypad4x1.Pin8, MH-ET_LIVE_ESP32_DEVKIT1.IO18
  N2: J1.pin2, Keypad4x1.Pin7, MH-ET_LIVE_ESP32_DEVKIT1.IO5
  N3: J1.pin3, Keypad4x1.Pin6, MH-ET_LIVE_ESP32_DEVKIT1.IO17
  N4: J1.pin4, Keypad4x1.Pin5, MH-ET_LIVE_ESP32_DEVKIT1.IO16
  N5: J1.pin5, Keypad4x1.Pin4, MH-ET_LIVE_ESP32_DEVKIT1.IO4
  N6: J1.pin6, Keypad4x1.Pin3, MH-ET_LIVE_ESP32_DEVKIT1.IO0
  N7: J1.pin7, Keypad4x1.Pin2, MH-ET_LIVE_ESP32_DEVKIT1.IO2
  N8: J1.pin8, Keypad4x1.Pin1, MH-ET_LIVE_ESP32_DEVKIT1.IO15
  3V3: MH-ET_LIVE_ESP32_DEVKIT1.3V3, J2.vcc
  GND: MH-ET_LIVE_ESP32_DEVKIT1.GND, J2.gnd

custom parts:
  Keypad Membran 4x4: Membrane Keypad 4x4 Matrix
  MH-ET LIVE ESP32 DEVKIT 38 pins: http://mh.nodebb.com/topic/2/mh-et-live-esp32-devkit
