# Fritzing sketch LCD IR (saved by Fritzing 0.9.3b)
breadboards: 1

parts:
  part = MH-ET LIVE ESP32 DEVKIT 38 pins
  LCD1 = LCD screen
  U1 = POT [package=pot_mammoth]
  Mod1 = KY-032 IR Obstacle Avoidance Sensor Module [package="Breakout board"]

nets:
  3V3: part.3V3, LCD1.VDD, LCD1.R/W, LCD1.LED+, U1.E, Mod1.+
  N1: part.IO34, Mod1.out
  GND: part.GND, LCD1.VSS, LCD1.LED-, U1.S, Mod1.GND
  N2: part.IO23, LCD1.RS
  N3: part.IO22, LCD1.E
  N4: part.IO4, LCD1.DB7
  N5: part.IO0, LCD1.DB6
  N6: part.IO2, LCD1.DB5
  N7: part.IO15, LCD1.DB4
  N8: LCD1.V0, U1.A

custom parts:
  MH-ET LIVE ESP32 DEVKIT 38 pins: http://mh.nodebb.com/topic/2/mh-et-live-esp32-devkit
  KY-032 IR Obstacle Avoidance Sensor Module: KY-032 Infrared Obstacle Avoidance Sensor. Distance-adjustable, infrared proximity sensor designed for wheeled robots. Also known as AD-032.
