# Fritzing sketch LDR_Buzzr (saved by Fritzing 0.9.3b)
breadboards: 1

parts:
  part = Resistor [tolerance=±5% resistance=220 package=THT]
  part_2 = LED - 5mm [color="Red (633nm)" package="5 mm [THT]"]
  part_3 = Piezo Speaker
  part_4 = MH-ET LIVE ESP32 DEVKIT 38 pins
  part_5 = Photocell (LDR) [package=THT]
  part_6 = Resistor [tolerance=±5% resistance=220 package="2010 [SMD]"]

nets:
  N1: part.Pin_0, part_3.pin1, part_3.pin2, part_4.GND, part_4.IO18, part_5.pin_1
  N2: part.Pin_1, part_2.cathode
  N3: part_2.anode, part_4.IO2
  N4: part_4.3V3, part_6.Pin_0
  N5: part_4.IO34, part_5.pin_0, part_6.Pin_1

custom parts:
  MH-ET LIVE ESP32 DEVKIT 38 pins: http://mh.nodebb.com/topic/2/mh-et-live-esp32-devkit
