# Fritzing sketch Gas (saved by Fritzing 0.9.3b)
breadboards: 1

parts:
  part = MH-ET LIVE ESP32 DEVKIT 38 pins
  U1 = GAS_SENSOR [package=mq-3]
  J1 = Piezo Speaker
  LED1 = LED - 5mm [color="Red (633nm)" package="5 mm [THT]"]
  R1 = Resistor [tolerance=±5% resistance=220 package=THT]

nets:
  N1: part.IO22, LED1.anode
  N2: part.IO21, J1.pin2
  N3: part.IO15, U1.B1
  N4: U1.H1, U1.H2, J1.pin1, R1.Pin_1
  N5: LED1.cathode, R1.Pin_0

custom parts:
  MH-ET LIVE ESP32 DEVKIT 38 pins: http://mh.nodebb.com/topic/2/mh-et-live-esp32-devkit
