# Fritzing sketch Push_Color (saved by Fritzing 0.9.3b)
breadboards: 1

parts:
  part = MH-ET LIVE ESP32 DEVKIT 38 pins
  LED1 = smd LED [color="Red (633nm)" package="0603 [SMD]"]
  R1 = Resistor [tolerance=±5% resistance=220 package="0805 [SMD]"]
  Button = Momentary Switch [package=ksa_sealed_tac_switch]
  R2 = Resistor [tolerance=±5% resistance=220 package="0805 [SMD]"]

nets:
  N1: part.IO35, Button.2
  N2: part.IO32, LED1.anode
  N3: LED1.cathode, R1.Pin_1
  N4: R1.Pin_0, R2.Pin_0
  N5: Button.4, R2.Pin_1

custom parts:
  MH-ET LIVE ESP32 DEVKIT 38 pins: http://mh.nodebb.com/topic/2/mh-et-live-esp32-devkit
