# Fritzing sketch rainSensor (saved by Fritzing 0.9.3b)
breadboards: 1

parts:
  YL-83_-_Control_Board1 = YL-83 Rain Sensor - Control Board
  YL-83_-_Detection_Board1 = YL-83 Rain Sensor - Detection Board
  MH-ET_LIVE_ESP32_DEVKIT1 = MH-ET LIVE ESP32 DEVKIT 38 pins

nets:
  VCC: YL-83_-_Control_Board1.VCC, MH-ET_LIVE_ESP32_DEVKIT1.5V
  GND: YL-83_-_Control_Board1.GND, MH-ET_LIVE_ESP32_DEVKIT1.GND
  N1: YL-83_-_Control_Board1.AO, MH-ET_LIVE_ESP32_DEVKIT1.IO13
  N2: YL-83_-_Control_Board1.POS, YL-83_-_Detection_Board1.POS
  N3: YL-83_-_Control_Board1.NEG, YL-83_-_Detection_Board1.NEG

custom parts:
  YL-83 Rain Sensor - Control Board: The YL-83 is a rain sensor that has more resistance when dry and less resistance when wet. The module runs at 5V.
  YL-83 Rain Sensor - Detection Board: The YL-83 is a rain sensor that has more resistance when dry and less resistance when wet. The module runs at 5V.
  MH-ET LIVE ESP32 DEVKIT 38 pins: http://mh.nodebb.com/topic/2/mh-et-live-esp32-devkit
